# Fritzing sketch tft_lcd_spi_st7735 (saved by Fritzing 0.9.6b)
circuit board: 8.46667cm x 5.64444cm

parts:
  Pico_H2 = Raspberry Pi Pico H
  LCD1 = 1_7in tft lcd

nets:
  N1: Pico_H2.VSYS, LCD1.pin2
  N2: Pico_H2.GND, LCD1.pin_1, LCD1.pin_14
  N3: Pico_H2.3V3, LCD1.pin_8
  N4: Pico_H2.GP19, LCD1.pin4
  N5: Pico_H2.GP18, LCD1.pin3
  N6: Pico_H2.GP17, LCD1.pin_5
  N7: Pico_H2.GP3, LCD1.pin_6
  N8: Pico_H2.GP2, LCD1.pin_7

custom parts:
  Raspberry Pi Pico H: Raspberry Pi Pico H. Based around the RP2040 microcontroller the Pico H is a low cost microcontroller device bringing Raspberry Pi quality, cost, and easy of use to the microcontroller space.
  1_7in tft lcd: This is the Zoll 1.77in spi lcd display. The 1.77" display has 128x160 color pixels.
